# Fritzing sketch ANS Circuit (saved by Fritzing 0.9.3b)

parts:
  A1 = Raspberry Pi 5
  Part1 = Arduino Nano (Rev3.0) (ICSP)
  USBTTL1 = USB A Plug
  USBTTL3 = Micro USB B Plug
  USBTTL4 = USB A Plug
  USBTTL5 = USB A Plug
  USBTTL6 = USB A Plug
  Part2 = 9-DOF Absolute Orientation IMU Fusion Breakout - BNO055
  DC_Mot_Enc1 = DC Motor with two-phase hall-encoder [part_number=VT-E-G25A-06-177E]
  BAT1 = Lithium Ion Polymer Battery 11.1v 5000mah
  A2 = MD30C
  Part3 = Arduino Nano (Rev3.0) (ICSP)
  USBTTL7 = Micro USB B Plug
  DC_Mot_Enc2 = DC Motor with two-phase hall-encoder [part_number=VT-E-G25A-06-177E]
  A3 = MD30C
  Part4 = Arduino Nano (Rev3.0) (ICSP)
  USBTTL8 = Micro USB B Plug
  DC_Mot_Enc3 = DC Motor with two-phase hall-encoder [part_number=VT-E-G25A-06-177E]
  A4 = MD30C
  M1 = RPlidar A1M8 [package=THT]  # not connected
  USBTTL9 = Micro USB B Plug

nets:
  N1: A1.5V, Part2.5.0V
  N2: A1.GPIO2, Part2.SDA_5V
  N3: A1.GPIO3, Part2.SCL_5V
  GND: A1.GND, Part2.GND, Part2.PS0_3V, Part2.PS1_3V
  GND_2: Part1.GND, DC_Mot_Enc1.pin4, BAT1.negative, A2.pin_2, A2.pin_3, Part3.GND, DC_Mot_Enc2.pin4, A3.pin_2, A3.pin_3, Part4.GND, DC_Mot_Enc3.pin4, A4.pin_2, A4.pin_3
  N4: Part1.D2, DC_Mot_Enc1.pin5
  N5: Part1.D3, DC_Mot_Enc1.pin6
  N6: Part1.D5, A2.pin_4
  N7: Part1.D6, A2.pin_5
  N8: Part1.5V, Part1.A5, DC_Mot_Enc1.pin3
  N9: USBTTL1.usb, USBTTL7.usb
  N10: USBTTL3.usb, USBTTL4.usb
  N11: USBTTL5.usb, USBTTL9.usb
  N12: USBTTL6.usb, USBTTL8.usb
  N13: DC_Mot_Enc1.pin1, A2.pin_20
  N14: DC_Mot_Enc1.pin2, A2.pin_19
  N15: BAT1.positive, A2.pin_1, A3.pin_1, A4.pin_1
  N16: Part3.D2, DC_Mot_Enc2.pin5
  N17: Part3.D3, DC_Mot_Enc2.pin6
  N18: Part3.D5, A3.pin_4
  N19: Part3.D6, A3.pin_5
  N20: Part3.5V, Part3.A5, DC_Mot_Enc2.pin3
  N21: DC_Mot_Enc2.pin1, A3.pin_20
  N22: DC_Mot_Enc2.pin2, A3.pin_19
  N23: Part4.D2, DC_Mot_Enc3.pin5
  N24: Part4.D3, DC_Mot_Enc3.pin6
  N25: Part4.D5, A4.pin_4
  N26: Part4.D6, A4.pin_5
  N27: Part4.5V, DC_Mot_Enc3.pin3
  N28: DC_Mot_Enc3.pin1, A4.pin_20
  N29: DC_Mot_Enc3.pin2, A4.pin_19

custom parts:
  Raspberry Pi 5: The RPi5, a faster version of the awesome Raspberry Pi4B ARM Board with 40 pin gpio.
  9-DOF Absolute Orientation IMU Fusion Breakout - BNO055: A MEMS accelerometer, magnetometer and gyroscope on a single die with a high speed ARM Cortex-M0 based processor to digest all the sensor data, abstract the sensor fusion and real time requirements away, and spit out data you can use in quaternions, Euler angles or vectors.
  RPlidar A1M8: .The RPLIDAR A1 is the next generation low cost 360 degree 2D laser scanner (LIDAR) solution developed by SLAMTEC. It can take up to 4000 samples of laser ranging per second with high rotation speed. And equipped with SLAMTEC patented OPTMAG technology, it breakouts the life limitation of traditional LIDAR system so as to work stably for a long time.
